# Fritzing sketch scma (saved by Fritzing 0.8.5b)
breadboards: 1

parts:
  Raspberry_Pi_B_rev1 = Raspberry Pi B rev2
  IC1 = L293D [package=THT]
  M1 = DC Motor
  M2 = DC Motor
  VCC1 = 4 x AAA Battery Mount

nets:
  N1: Raspberry_Pi_B_rev1.5V, IC1.+V
  N2: Raspberry_Pi_B_rev1.GPIO_23, IC1.In_2
  N3: Raspberry_Pi_B_rev1.GPIO_22, IC1.Enable_2
  N4: Raspberry_Pi_B_rev1.GPIO_24, IC1.In_1
  N5: Raspberry_Pi_B_rev1.GPIO_9, IC1.In_3
  N6: Raspberry_Pi_B_rev1.GPIO_25, IC1.Enable_1
  N7: Raspberry_Pi_B_rev1.GPIO_11, IC1.In_4
  N8: Raspberry_Pi_B_rev1.GND, IC1.0V, VCC1.-
  N9: IC1.Out_1_(_Controlled_by_Enable_1_), M2.pin_2
  N10: IC1.Out_2_(_Controlled_by_Enable_1_), M2.pin_1
  N11: IC1.+Vmotor, VCC1.+
  N12: IC1.Out_3_(_Controlled_by_Enable_2_), M1.pin_2
  N13: IC1.Out_4_(_Controlled_by_Enable_2_), M1.pin_1
